# Fritzing sketch blazing-baton (saved by Fritzing 0.9.4)
breadboards: 1

parts:
  Bauteil2 = NRF24L01+ Breakout Board
  Bauteil3 = NanoESP
  R1 = Resistor [tolerance=±5% resistance=4.7k package="0603 [SMD]"]
  IC2 = 6n137 Optocoupler [package="DIP (Dual Inline) [THT]"]
  R4 = Resistor [tolerance=±5% resistance=220 package="0603 [SMD]"]
  D2 = Schottky Diode [part_number=1N5817 package="300 mil [THT]"]
  R5 = Resistor [tolerance=±5% resistance=220 package="0603 [SMD]"]
  DIN2 = DIN-5 jack (MIDI) [package=THT]
  C1 = Capacitor Polarized [package=panasonic_c]
  NEOPIXEL1 = Neopixel Strip -- Black (30/m)

nets:
  GND: Bauteil2.GND, Bauteil3.GND, R1.Pin_1, IC2.GND, C1.+, NEOPIXEL1.GND
  VCC: Bauteil2.VCC, Bauteil3.3V3, C1.-
  N1: Bauteil2.CE, Bauteil3.D10
  N2: Bauteil2.CS, Bauteil3.D9
  N3: Bauteil2.SCK, Bauteil3.D13/SCK
  N4: Bauteil2.MOSI, Bauteil3.D11/MOSI
  N5: Bauteil2.MISO, Bauteil3.D12/MISO
  N6: Bauteil3.D0/RX, IC2.Vo, R5.Pin_1
  N7: Bauteil3.D6, NEOPIXEL1.DI
  5V: Bauteil3.5V, R5.Pin_0, NEOPIXEL1.+5V
  N8: R1.Pin_0, IC2.Ve
  N9: IC2.Vf+, R4.Pin_1, D2.cathode
  N10: IC2.Vf-, D2.anode, DIN2.4
  N11: R4.Pin_0, DIN2.5

notes:
  Opto-isolator Circuit
  Fairchild 6n137 fast opto-coupler, 10Mbits/s rated
  Reverse protection diode is shottky with 30V or higher rating (1N5818 is 30V peak, 1A part)
  Input capacitor C1 should be 30V rated or higher
  Input LED forward voltage ~1.4V typ at 10mA forward current
  1MHz noise cutoff using input RC Low Pass filter, with 0.4us rise time
  Input current limit resistor is two 0.25W 3.3k resistors in parallel
  1.65k delivers
  ~9mA from 15V,
  ~15mA max at rated input voltage
  ~3.7mA at low input of 7V
  max power 300mW in input resistors at max voltage
  Larger input resistor can be used at expense of raising low end input voltage limit for reliable operation
  High level output current max 20uA results in 20mV offset
  Input threshold approx 2.5mA with 1k load resistor
  Designed for inputs of between 7V and 24V, 12-15V nominal
  Ve is for strobing the output and can be left NC if not used as has internal pullup
  Output resistor allows for full output low voltage at >5mA output current
  0.1uF Vcc decoupling required close to Vcc and GND pins
  For connection to Raspberry Pi use a level converter to convert from 5V logic to 3.3V.
  Input 7V to 24V, 15V nominal, 500kHz
  Note that grounds are not joined between source and circuit.
  Example use:
  DCC decoder front end isolator feeding Arduino
  This work by hobbyistdave is licensed under a Creative Commons Attribution-ShareAlike 4.0 International License
  No warranty either express or implied is given.
  This schematic was created with Fritzing.
  Inspired by Geoff Bunza at
  http://model-railroad-hobbyist.com/node/19446
  NRF24L01
  10µF
  220 Ω
  4.7kΩ
  DIN MIDI IN
  1N914
  16 RGB LEDs (Adafruit NeoPixel Strip)
  6N138

custom parts:
  6n137 Optocoupler: 6n137 fast Optocoupler. With 8 pins on a 300mil dual inline package (DIP) footprint. Ve is strobe input. Output is inverting.
  Neopixel Strip -- Black (30/m): Neopixel Strip, Black, 30 pixels per meter.
